# Fritzing sketch arduino_DS18B20 (saved by Fritzing 0.9.3b)

parts:
  Part1 = Arduino Uno (Rev3)
  DS1 = DS18B20 1-Wire Temperature Sensor [part_number=DS18B20]
  R1 = Resistor [tolerance=±5% resistance=4.7k package="2010 [SMD]"]

nets:
  N1: Part1.D2, DS1.DQ, R1.Pin_1
  5V: Part1.5V, DS1.VDD
  GND: Part1.GND, DS1.GND

notes:
  DS18B20
  >GND
  >DATA
  >VCC
  4.7kΩ
