# Fritzing sketch arduino_GY-521_MPU-6050 (saved by Fritzing 0.9.3b)

parts:
  Part1 = Arduino Mega 2560 (Rev3)
  GY1 = GY-521 (MPU-6050) [form="♀ (female)" package=THT]

nets:
  N1: Part1.SCL, GY1.pin3
  N2: Part1.SDA, GY1.pin4
  N3: Part1.5V, GY1.pin1
  N4: Part1.GND, GY1.pin2
  N5: Part1.D2_PWM, GY1.pin8

custom parts:
  GY-521 (MPU-6050): Placa GY-521 basada en conjunto de acelerómetro+giroscopios MPU-6050
