# Fritzing sketch arduino_GY-91_MPU-9250_BMP280 (saved by Fritzing 0.9.3b)

parts:
  Part1 = Arduino Mega 2560 (Rev3)
  GY1 = GY-521 (MPU-6050) [form="♀ (female)" package=THT]

nets:
  N1: Part1.D21/SCL, GY1.pin4
  N2: Part1.D20/SDA, GY1.pin5
  N3: Part1.5V, GY1.pin1
  N4: Part1.GND, GY1.pin3

notes:
  GY-91
  (MPU-9250 + BMP280)
  Arduino -------------- GY-91
  5V ———————- VIN
  SDA (Pin 20) ——— SDA
  SCL (Pin 21) ———- SCL
  GND ——————- GND

custom parts:
  GY-521 (MPU-6050): Placa GY-521 basada en conjunto de acelerómetro+giroscopios MPU-6050
