# Fritzing sketch arduino_MQ (saved by Fritzing 0.9.3b)

parts:
  Part1 = Arduino Uno (Rev3) - ICSP
  Part2 = MQ-3 breakout
  Part3 = MQ-3 breakout

nets:
  N1: Part1.A0, Part2.AO
  N2: Part1.A1, Part3.AO
  5V: Part1.5V, Part2.VCC
  GND: Part1.GND, Part2.GND

notes:
  MQ-2

custom parts:
  MQ-3 breakout: Alcohol sensor is capable of detecting alcohol (ethanol) particles on itself and gives the information in digital form back to us to manipulate with it. SKU:101251 • Voltage: 5V DC • Power: max 750mW • Measurement range: 0.04-4mg/L
