# Fritzing sketch arduino_PIR (saved by Fritzing 0.9.3b)

parts:
  Part1 = Arduino Uno (Rev3) - ICSP
  PIR1 = PIR sensor

nets:
  N1: Part1.D8, PIR1.SIG
  5V: Part1.5V, PIR1.VDD
  GND: Part1.GND, PIR1.GND
