# Fritzing sketch arduino_RTC_DS1302 (saved by Fritzing 0.9.3b)

parts:
  Part1 = Arduino Mega 2560 (Rev3)
  PCB2 = RTC_DS1302_module

nets:
  N1: Part1.D8_PWM, PCB2.RST
  5V: Part1.5V, PCB2.VCC
  GND: Part1.GND, PCB2.GND
  N2: Part1.D6_PWM, PCB2.CLK
  N3: Part1.D7_PWM, PCB2.DAT

custom parts:
  RTC_DS1302_module: Arduino module DS1302 SPI Real Time Clock
