# Fritzing sketch arduino_VL6180 (saved by Fritzing 0.9.3b)
breadboards: 1

parts:
  Part1 = Arduino Uno (Rev3)
  U1 = Voltage Regulator [package=to220-adj]
  R1 = Resistor [tolerance=±5% resistance=240 package="0603 [SMD]"]
  R2 = Resistor [tolerance=±5% resistance=300 package="0603 [SMD]"]
  VL6181 = Adafruit VL6180X Time of Flight Distance Sensor [part_number="Adafruit #3316"]

nets:
  N1: Part1.A4/SDA, VL6181.SDA
  N2: Part1.A5/SCL, VL6181.SCL
  N3: Part1.5V, U1.OUT
  GND: Part1.GND, R2.Pin_0, VL6181.GND
  N4: U1.ADJ, R1.Pin_0, R2.Pin_1
  N5: U1.IN, R1.Pin_1, VL6181.2.8V

notes:
  LM317
  240Ω
  300Ω
  Note: Connect to 5 V
  Depending on VL6180 breakout, pins order might differ

custom parts:
  Adafruit VL6180X Time of Flight Distance Sensor: The VL6180X is a Time of Flight distance sensor like no other you've used! The sensor contains a very tiny invisible laser source, and a matching sensor. The VL6180X can detect the "time of flight", or how long the light has taken to bounce back to the sensor. Since it uses a very narrow light source, it is good for determining distance of only the surface directly in front of it. Unlike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
