# Fritzing sketch arduino_capacitive_module (saved by Fritzing 0.9.3b)

parts:
  Part1 = Arduino Mega 2560 (Rev3)
  TTP223B1 = TTP223B Capacitive Touch Sensor Module

nets:
  5V: Part1.5V, TTP223B1.VCC
  GND: Part1.GND, TTP223B1.GND
  N1: Part1.D2_PWM, TTP223B1.SIG

custom parts:
  TTP223B Capacitive Touch Sensor Module: The TTP223B capacitive touch sensor module uses the TTP223B IC. The appropriate voltage is approximately 2 to 5.5 volts.
