# Fritzing sketch arduino_limit_switch (saved by Fritzing 0.9.3b)

parts:
  Part1 = Arduino Uno (Rev3) - ICSP
  S1 = Toggle Switch [package=THT]

nets:
  N1: Part1.GND, S1.L2
  N2: Part1.D2, S1.COM

notes:
  Limit switch pins: NC, NO, COM
