# Fritzing sketch arduino_microSD_card (saved by Fritzing 0.9.3b)

parts:
  Part1 = Arduino Mega 2560 (Rev3)
  Part2 = MicroSD Card Module

nets:
  5V: Part1.5V, Part2.VCC
  GND: Part1.GND, Part2.GND
  N1: Part1.D50, Part2.MISO
  N2: Part1.D51, Part2.MOSI
  N3: Part1.D52, Part2.SCK
  N4: Part1.D53, Part2.CS

notes:
  Wiring (depends on SPI pins)
  SD card module Arduino Uno Arduino Mega
  VCC 5V 5V
  CS 4 53
  MOSI 11 51
  CLK 13 52
  MISO 12 50
  GND GND GND
