# Fritzing sketch arduino_photocell (saved by Fritzing 0.9.3b)

parts:
  Part1 = Arduino Uno (Rev3) - ICSP
  R1 = PHOTOCELL [package=photocell]
  R2 = Resistor [tolerance=±5% resistance=10k package="2010 [SMD]"]

nets:
  N1: Part1.A0, R1.P$1, R2.Pin_1
  N2: Part1.5V, R1.P$2
  N3: Part1.GND, R2.Pin_0

notes:
  10k resistor
