# Fritzing sketch arduino_potentiometer (saved by Fritzing 0.9.3b)

parts:
  Part1 = Arduino Uno (Rev3) - ICSP
  R2 = Rotary Potentiometer (Small) [maximum_resistance=100kΩ package=THT]

nets:
  N1: Part1.A0, R2.wiper
  N2: Part1.5V, R2.leg2
  N3: Part1.GND, R2.leg1

notes:
  Note: switching the position of the GND and 5V pins on the pot will result in a shift of values read vs direction (i.e. turn the knob clockwise to turn the signal down)
