# Fritzing sketch arduino_rotary_encoder (saved by Fritzing 0.9.3b)

parts:
  Part1 = Arduino Uno (Rev3) - ICSP
  ENCODER1 = Rotary Encoder with Knob

nets:
  N1: Part1.GND, ENCODER1.no_name_yet#2
  N2: Part1.D2, ENCODER1.no_name_yet#3
  N3: Part1.D3_PWM, ENCODER1.no_name_yet#1
  N4: Part1.D4, ENCODER1.no_name_yet#4

custom parts:
  Rotary Encoder with Knob: Rotary Encoder with 1/4" Shaft and Knob
